# Fritzing sketch LM35-LM358 (saved by Fritzing 0.8.7b)
breadboards: 1

parts:
  U1 = LM358 [package=dip08]
  VCC1 = Battery
  T1 = LM35 Temperature Sensor [package="TO92 [THT]"]
  R1 = Resistor [tolerance=±5% resistance=1k package=THT]
  R2 = Resistor [tolerance=±5% resistance=10k package=THT]

nets:
  N1: U1.G$1_OUT, R2.Pin_1
  N2: U1.G$1_-IN, R1.Pin_1, R2.Pin_0
  N3: U1.G$1_+IN, T1.Vout
  N4: U1.G$1_V-, VCC1.-, T1.GND, R1.Pin_0
  N5: U1.G$1_V+, VCC1.+, T1.+Vs
