# Fritzing sketch SensorTemperatura (saved by Fritzing 0.8.5b)
breadboards: 1

parts:
  T1 = LM35 Temperature Sensor [package="TO92 [THT]"]
  V1 = DC Power [voltage=5V frequency=60]

nets:
  N1: T1.+Vs, V1.V+
  N2: T1.GND, V1.V-
