# Fritzing sketch SensorTemperaturaAcondicionadoLM358Invertido (saved by Fritzing 0.8.5b)
breadboards: 1

parts:
  T1 = LM35 Temperature Sensor [package="TO92 [THT]"]
  V1 = DC Power [voltage=5V frequency=60]
  U1 = LM 358 Dual Op-Amp [package="DIP8 [THT]"]
  R1 = Resistor [tolerance=±5% resistance=10k package=THT]
  R2 = Resistor [tolerance=±5% resistance=1k package=THT]
  R3 = Resistor [tolerance=±5% resistance=1k package=THT]

nets:
  N1: T1.+Vs, V1.V+, U1.connector7, R3.Pin_1
  N2: T1.Vout, R2.Pin_0
  N3: T1.GND, V1.V-, U1.connector3
  N4: U1.connector0, R1.Pin_1
  N5: U1.connector1, R1.Pin_0, R2.Pin_1
  N6: U1.connector2, R3.Pin_0
