# Fritzing sketch ControlPID (saved by Fritzing 0.9.0b)
breadboards: 1

parts:
  Parte1 = Arduino Uno (Rev3)
  R2 = Trimmer Potentiometer [maximum_resistance=10kΩ package=THT]
  R3 = Trimmer Potentiometer [maximum_resistance=10kΩ package=THT]
  R1 = Trimmer Potentiometer [maximum_resistance=10kΩ package=THT]

nets:
  N1: Parte1.A0, R1.wiper
  N2: Parte1.A1, R2.wiper
  N3: Parte1.A2, R3.wiper
  N4: Parte1.5V, R2.leg2, R3.leg2, R1.leg2
  N5: Parte1.GND, R2.leg1, R3.leg1, R1.leg1
